# Fritzing sketch BreadBoard (saved by Fritzing 0.9.3b)
breadboards: 1

parts:
  IC1 = L293D [package=THT]
  U1 = NodeMCU V3.0
  Power_plug1 = Power plug
  M1 = DC Motor
  U2 = Chip antenna [package=antenna-chip]
  ANT1 = Antenna

nets:
  N1: IC1.Enable_1, U1.D5
  N2: IC1.In_1, U1.D6
  N3: IC1.Out_1_(_Controlled_by_Enable_1_), M1.pin_2
  N4: IC1.0V, Power_plug1.GND
  N5: IC1.Out_2_(_Controlled_by_Enable_1_), M1.pin_1
  N6: IC1.In_2, U1.D7
  N7: IC1.+Vmotor, Power_plug1.VCC
  N8: IC1.+V, U1.Vin
  N9: U1.3V3, U2.SIGNAL
  N10: U1.GND#6, U1.GND#13, U1.GND#16, U1.GND#33, U2.GND, ANT1.antenna_lead

notes:
  RF433 Transmitter

custom parts:
  NodeMCU V3.0: ESP8266 based NodeMCU
